# Fritzing sketch gerador_ad9833_versao_2 (saved by Fritzing 0.9.3b)
breadboards: 1

parts:
  arduino_nano = Arduino Nano (Rev3.0)
  GND_5V = female pin header, 2 pins [form="♀ (female)"]
  C1 = Ceramic Capacitor [capacitance=100nF package="100 mil [THT, multilayer]"]
  R1 = Resistor [tolerance=±5% resistance=680k package=THT]
  trimpot = TRIMPOT [package=3386u]
  R3 = Resistor [tolerance=±5% resistance=1k package=THT]
  1=gnd_2=saida_modulo_3=saida_filtro_PA_4=saida_seguidor_5=saida_seguidor-alternativo_6=saida_ganho = female pin header, 6 pins [form="♀ (female)"]
  3_3v = female pin header, 1 pin [form="♀ (female)"]
  IC1 = TL072 [package="DIP (Dual Inline) [THT]"]
  part = TL072 [package="DIP (Dual Inline) [THT]"]
  IC1_1 = TL072 [package="DIP (Dual Inline) [THT]"]
  IC1_2 = TL072 [package="DIP (Dual Inline) [THT]"]
  1=Sin_2=PA_in = female pin header, 2 pins [form="♀ (female)"]
  1=PA_out_2=Seg_in = female pin header, 2 pins [form="♀ (female)"]
  IC2 = TL072 [package="DIP (Dual Inline) [THT]"]
  part_2 = TL072 [package="DIP (Dual Inline) [THT]"]
  IC2_1 = TL072 [package="DIP (Dual Inline) [THT]"]
  IC2_2 = TL072 [package="DIP (Dual Inline) [THT]"]
  1=Seg_out_2=Gain_in = female pin header, 2 pins [form="♀ (female)"]
  1=PA_out_2=SegAlt_in = female pin header, 2 pins [form="♀ (female)"]
  1=SegAlt_out_2=Gain_in = female pin header, 2 pins [form="♀ (female)"]
  1=-V_2=+V = female pin header, 2 pins [form="♀ (female)"]
  1=UART_IN_2=UART_OUT = female pin header, 2 pins [form="♀ (female)"]
  1=I2C_CLK_2=I2C_DATA = female pin header, 2 pins [form="♀ (female)"]
  1=SPI_SCK_2=SPI_MISO_3=SPI_MOSI_4=SPI_SS = female pin header, 4 pins [form="♀ (female)"]
  GND_5V_2 = female pin header, 2 pins [form="♀ (female)"]
  1=Vcc_2=DGND_3=SDATA_4=SCLK_5=FSYNC_6=AGND_7=OUT = female pin header, 7 pins [form="♀ (female)"]
  1-Sin_Gain_2=gnd = female pin header, 2 pins [form="♀ (female)"]

nets:
  N1: arduino_nano.D1/TX, 1=UART_IN_2=UART_OUT.pin2
  N2: arduino_nano.D0/RX, 1=UART_IN_2=UART_OUT.pin1
  GND: arduino_nano.GND, GND_5V.pin1, R1.Pin_1, R3.Pin_1, 1=gnd_2=saida_modulo_3=saida_filtro_PA_4=saida_seguidor_5=saida_seguidor-alternativo_6=saida_ganho.pin1, GND_5V_2.pin1, 1=Vcc_2=DGND_3=SDATA_4=SCLK_5=FSYNC_6=AGND_7=OUT.pin2, 1=Vcc_2=DGND_3=SDATA_4=SCLK_5=FSYNC_6=AGND_7=OUT.pin6, 1-Sin_Gain_2=gnd.pin2
  N3: arduino_nano.D9, 1=Vcc_2=DGND_3=SDATA_4=SCLK_5=FSYNC_6=AGND_7=OUT.pin5
  N4: arduino_nano.D10, 1=SPI_SCK_2=SPI_MISO_3=SPI_MOSI_4=SPI_SS.pin4
  N5: arduino_nano.D11/MOSI, 1=SPI_SCK_2=SPI_MISO_3=SPI_MOSI_4=SPI_SS.pin3, 1=Vcc_2=DGND_3=SDATA_4=SCLK_5=FSYNC_6=AGND_7=OUT.pin3
  N6: arduino_nano.D12/MISO, 1=SPI_SCK_2=SPI_MISO_3=SPI_MOSI_4=SPI_SS.pin2
  N7: arduino_nano.5V, GND_5V.pin2
  N8: arduino_nano.A5, 1=I2C_CLK_2=I2C_DATA.pin1
  N9: arduino_nano.A4, 1=I2C_CLK_2=I2C_DATA.pin2
  N10: arduino_nano.3V3, 3_3v.pin1
  N11: arduino_nano.D13/SCK, 1=SPI_SCK_2=SPI_MISO_3=SPI_MOSI_4=SPI_SS.pin1, 1=Vcc_2=DGND_3=SDATA_4=SCLK_5=FSYNC_6=AGND_7=OUT.pin4
  N12: C1.0, R1.Pin_0, 1=gnd_2=saida_modulo_3=saida_filtro_PA_4=saida_seguidor_5=saida_seguidor-alternativo_6=saida_ganho.pin3, 1=PA_out_2=Seg_in.pin1, 1=PA_out_2=SegAlt_in.pin1
  N13: C1.1, 1=Sin_2=PA_in.pin2
  N14: trimpot.CCW, trimpot.WIPER, R3.Pin_0, IC2.connector1, IC2_1.pin2
  N15: trimpot.CW, 1=gnd_2=saida_modulo_3=saida_filtro_PA_4=saida_seguidor_5=saida_seguidor-alternativo_6=saida_ganho.pin6, IC2.connector0, IC2_1.pin1, 1-Sin_Gain_2=gnd.pin1
  N16: 1=gnd_2=saida_modulo_3=saida_filtro_PA_4=saida_seguidor_5=saida_seguidor-alternativo_6=saida_ganho.pin2, 1=Sin_2=PA_in.pin1, 1=Vcc_2=DGND_3=SDATA_4=SCLK_5=FSYNC_6=AGND_7=OUT.pin7
  N17: 1=gnd_2=saida_modulo_3=saida_filtro_PA_4=saida_seguidor_5=saida_seguidor-alternativo_6=saida_ganho.pin4, IC1.connector0, IC1.connector1, IC1_1.pin1, IC1_1.pin2, 1=Seg_out_2=Gain_in.pin1
  N18: 1=gnd_2=saida_modulo_3=saida_filtro_PA_4=saida_seguidor_5=saida_seguidor-alternativo_6=saida_ganho.pin5, IC2.connector5, IC2.connector6, IC2_2.pin6, IC2_2.pin7, 1=SegAlt_out_2=Gain_in.pin1
  N19: IC1.connector2, IC1_1.pin3, 1=PA_out_2=Seg_in.pin2
  N20: IC1.connector3, part.pin4, IC2.connector3, part_2.pin4, 1=-V_2=+V.pin1
  N21: IC1.connector5, IC1.connector6
  N22: IC1.connector7, part.pin8, IC2.connector7, part_2.pin8, 1=-V_2=+V.pin2
  N23: IC1_2.pin6, IC1_2.pin7
  N24: IC2.connector2, IC2_1.pin3, 1=Seg_out_2=Gain_in.pin2, 1=SegAlt_out_2=Gain_in.pin2
  N25: IC2.connector4, IC2_2.pin5, 1=PA_out_2=SegAlt_in.pin2
  N26: GND_5V_2.pin2, 1=Vcc_2=DGND_3=SDATA_4=SCLK_5=FSYNC_6=AGND_7=OUT.pin1

custom parts:
  TL072: Dual Operational Amplifier
  TL072: Dual Operational Amplifier
  TL072: Dual Operational Amplifier
  TL072: Dual Operational Amplifier
